# Fritzing sketch AT circuit (saved by Fritzing 0.9.3b)
breadboards: 2

parts:
  S1 = Pushbutton [package="[THT]"]
  S2 = Pushbutton [package="[THT]"]
  S3 = Pushbutton [package="[THT]"]
  S4 = Pushbutton [package="[THT]"]
  S5 = Pushbutton [package="[THT]"]
  Part1 = Arduino Uno (Rev3)
  LED1 = LED - 5mm [color="Red (633nm)" package="5 mm [THT]"]
  R1 = Resistor [tolerance=±5% resistance=220 package=THT]
  Часть1 = Arduino Nano (Rev3.0)
  S6 = Pushbutton [package="[THT]"]
  S7 = Pushbutton [package="[THT]"]
  S8 = Pushbutton [package="[THT]"]
  S9 = Pushbutton [package="[THT]"]
  S10 = Pushbutton [package="[THT]"]

nets:
  N1: S1.Pin_1, S1.Pin_2, S2.Pin_3, S2.Pin_4, S3.Pin_3, S3.Pin_4, S4.Pin_3, S4.Pin_4, S5.Pin_3, S5.Pin_4, Part1.GND
  N2: S1.Pin_3, S1.Pin_4, Part1.A0
  N3: S2.Pin_1, S2.Pin_2, Part1.A1
  N4: S3.Pin_1, S3.Pin_2, Part1.A2
  N5: S4.Pin_1, S4.Pin_2, Part1.A3
  N6: S5.Pin_1, S5.Pin_2, Part1.A4/SDA
  N7: Part1.5V, LED1.cathode, R1.Pin_0
  N8: LED1.anode, R1.Pin_1
  N9: Часть1.GND, S6.Pin_1, S6.Pin_2, S7.Pin_1, S7.Pin_2, S8.Pin_1, S8.Pin_2, S9.Pin_1, S9.Pin_2, S10.Pin_1, S10.Pin_2
  N10: Часть1.A4, S10.Pin_3, S10.Pin_4
  N11: Часть1.A3, S9.Pin_3, S9.Pin_4
  N12: Часть1.A2, S8.Pin_3, S8.Pin_4
  N13: Часть1.A1, S7.Pin_3, S7.Pin_4
  N14: Часть1.A0, S6.Pin_3, S6.Pin_4
